// Logisim project Multiplication & Binary to BCD.circ as structural Verilog: 6 circuits, main circuit Multiplier
module Multiplier (
  input  [4:0] B,
  input  [4:0] A,
  output [7:0] Result,
  output Sign
);

  wire not_1_out, not_2_out, not_3_out, or_1_out, or_2_out, or_3_out, or_4_out, or_5_out, or_6_out, or_7_out,
       xor_1_out;
  wire [2:0] and_2_out;
  wire [3:0] and_6_out, and_11_out, and_13_out, n4bit_adder_1_c, n4bit_adder_2_c;

  or or_1 (or_1_out, A[0], A[1]);
  and and_1 (Result[0], B[0], A[0]);
  and and_2 (and_2_out[0], B[0], A[1]);
  and and_3 (and_2_out[1], B[0], A[2]);
  and and_4 (and_2_out[2], B[0], A[3]);
  or or_2 (or_2_out, or_1_out, A[2]);
  or or_3 (or_3_out, or_2_out, A[3]);
  and and_5 (and_11_out[3], B[1], A[0]);
  and and_6 (and_6_out[0], B[2], A[0]);
  and and_7 (and_11_out[2], B[1], A[1]);
  and and_8 (and_6_out[1], B[2], A[1]);
  and and_9 (and_11_out[1], B[1], A[2]);
  and and_10 (and_6_out[2], B[2], A[2]);
  and and_11 (and_11_out[0], B[1], A[3]);
  and and_12 (and_6_out[3], B[2], A[3]);
  not not_1 (not_1_out, or_3_out);
  and and_13 (and_13_out[0], B[3], A[0]);
  and and_14 (and_13_out[1], B[3], A[1]);
  and and_15 (and_13_out[2], B[3], A[2]);
  and and_16 (and_13_out[3], B[3], A[3]);
  or or_4 (or_4_out, B[0], B[3]);
  or or_5 (or_5_out, or_4_out, B[2]);
  or or_6 (or_6_out, or_5_out, B[1]);
  not not_2 (not_2_out, or_6_out);
  _4Bit_adder u_4bit_adder_1 (
    .A({1'b0, and_2_out}), .B(and_11_out), .S0(Result[1]), .S1(n4bit_adder_1_c[3]), .S2(n4bit_adder_1_c[2]),
    .S3(n4bit_adder_1_c[1]), .C(n4bit_adder_1_c[0]));
  _4Bit_adder u_4bit_adder_2 (
    .A(and_6_out), .B(n4bit_adder_1_c), .S0(Result[2]), .S1(n4bit_adder_2_c[3]), .S2(n4bit_adder_2_c[2]),
    .S3(n4bit_adder_2_c[1]), .C(n4bit_adder_2_c[0]));
  _4Bit_adder u_4bit_adder_3 (
    .A(and_13_out), .B(n4bit_adder_2_c), .S0(Result[3]), .S1(Result[4]), .S2(Result[5]), .S3(Result[6]),
    .C(Result[7]));
  or or_7 (or_7_out, not_1_out, not_2_out);
  not not_3 (not_3_out, or_7_out);
  xor xor_1 (xor_1_out, B[4], A[4]);
  and and_17 (Sign, xor_1_out, not_3_out);
endmodule

// 4-Bit adder
module _4Bit_adder (
  input  [3:0] B,
  input  [3:0] A,
  output S0,
  output S1,
  output S2,
  output S3,
  output C
);

  wire fa_1_c, fa_2_c, fa_3_c;

  FA fa_1 (.A(A[0]), .B(B[3]), .Cin(1'b0), .S(S0), .C(fa_1_c));
  FA fa_2 (.A(B[2]), .B(A[1]), .Cin(fa_1_c), .S(S1), .C(fa_2_c));
  FA fa_3 (.A(B[1]), .B(A[2]), .Cin(fa_2_c), .S(S2), .C(fa_3_c));
  FA fa_4 (.A(A[3]), .B(B[0]), .Cin(fa_3_c), .S(S3), .C(C));
endmodule

module HA (
  input  A,
  input  B,
  output S,
  output COut
);

  xor Sum (S, A, B);
  and Carry_out (COut, A, B);
endmodule

module FA (
  input  A,
  input  B,
  input  Cin,
  output S,
  output C
);

  wire ha_1_cout, ha_1_s, ha_2_cout;

  HA ha_1 (.A(A), .B(B), .S(ha_1_s), .COut(ha_1_cout));
  HA ha_2 (.A(ha_1_s), .B(Cin), .S(S), .COut(ha_2_cout));
  or or_1 (C, ha_2_cout, ha_1_cout);
endmodule

module ADD3 (
  input  A0,
  input  A1,
  input  A2,
  input  A3,
  output out_5,
  output out_6,
  output out_7,
  output out_8
);

  wire and_1_out, and_2_out, and_3_out, and_4_out, and_5_out, and_6_out, and_7_out, and_8_out, and_9_out,
       and_10_out, and_11_out, and_12_out, and_13_out, not_1_out, not_2_out, not_3_out, not_4_out, or_1_out,
       or_2_out, or_4_out;

  not not_1 (not_1_out, A0);
  not not_2 (not_2_out, A3);
  not not_3 (not_3_out, A2);
  and and_1 (and_1_out, A0, not_3_out);
  not not_4 (not_4_out, A1);
  and and_2 (and_2_out, and_1_out, not_2_out);
  and and_3 (and_3_out, not_1_out, A1);
  and and_4 (and_4_out, not_1_out, A3);
  and and_5 (and_5_out, A0, A1);
  and and_6 (and_6_out, A1, not_3_out);
  and and_7 (and_7_out, not_1_out, A3);
  and and_8 (and_8_out, not_1_out, not_4_out);
  and and_9 (and_9_out, A0, A3);
  and and_10 (and_10_out, A2, A0);
  and and_11 (and_11_out, A1, A2);
  and and_12 (and_12_out, and_3_out, A2);
  and and_13 (and_13_out, and_8_out, A2);
  or or_1 (or_1_out, and_2_out, and_12_out);
  or or_2 (or_2_out, and_5_out, and_6_out);
  or or_3 (out_7, and_13_out, and_9_out);
  or or_4 (or_4_out, and_10_out, and_11_out);
  or or_5 (out_5, or_1_out, and_4_out);
  or or_6 (out_6, or_2_out, and_7_out);
  or or_7 (out_8, or_4_out, A3);
endmodule

module Convert_To_BCD (
  input  [7:0] in_1,
  output out_2,
  output out_3,
  output out_4,
  output out_5,
  output out_6,
  output out_7,
  output out_8,
  output out_9,
  output out_10,
  output out_11,
  output out_12,
  output out_13
);

  wire add3_1_out_5, add3_1_out_6, add3_1_out_7, add3_1_out_8, add3_2_out_5, add3_2_out_6, add3_2_out_7,
       add3_2_out_8, add3_3_out_5, add3_3_out_6, add3_3_out_7, add3_5_out_5, add3_5_out_6, add3_5_out_7,
       add3_5_out_8, add3_6_out_5, add3_6_out_6, add3_6_out_7, add3_6_out_8;

  ADD3 add3_1 (
    .A0(in_1[5]), .A1(in_1[6]), .A2(in_1[7]), .A3(1'b0), .out_5(add3_1_out_5), .out_6(add3_1_out_6),
    .out_7(add3_1_out_7), .out_8(add3_1_out_8));
  ADD3 add3_2 (
    .A0(in_1[4]), .A1(add3_1_out_5), .A2(add3_1_out_6), .A3(add3_1_out_7), .out_5(add3_2_out_5),
    .out_6(add3_2_out_6), .out_7(add3_2_out_7), .out_8(add3_2_out_8));
  ADD3 add3_3 (
    .A0(add3_5_out_8), .A1(add3_2_out_8), .A2(add3_1_out_8), .A3(1'b0), .out_5(add3_3_out_5),
    .out_6(add3_3_out_6), .out_7(add3_3_out_7), .out_8(out_4));
  ADD3 add3_4 (
    .A0(add3_6_out_8), .A1(add3_3_out_5), .A2(add3_3_out_6), .A3(add3_3_out_7), .out_5(out_8), .out_6(out_7),
    .out_7(out_6), .out_8(out_5));
  ADD3 add3_5 (
    .A0(in_1[3]), .A1(add3_2_out_5), .A2(add3_2_out_6), .A3(add3_2_out_7), .out_5(add3_5_out_5),
    .out_6(add3_5_out_6), .out_7(add3_5_out_7), .out_8(add3_5_out_8));
  ADD3 add3_6 (
    .A0(in_1[2]), .A1(add3_5_out_5), .A2(add3_5_out_6), .A3(add3_5_out_7), .out_5(add3_6_out_5),
    .out_6(add3_6_out_6), .out_7(add3_6_out_7), .out_8(add3_6_out_8));
  ADD3 add3_7 (
    .A0(in_1[1]), .A1(add3_6_out_5), .A2(add3_6_out_6), .A3(add3_6_out_7), .out_5(out_12), .out_6(out_11),
    .out_7(out_10), .out_8(out_9));

  assign out_2 = 1'b0;
  assign out_3 = 1'b0;
  assign out_13 = in_1[0];
endmodule
